// Logisim project sort.circ as structural Verilog: 3 circuits, main circuit main
module main (
  input  [7:0] x0,
  input  [1:0] sel0,
  input  en0,
  input  [1:0] sela,
  input  [7:0] x1,
  input  [1:0] sel1,
  input  en1,
  input  [1:0] selb,
  input  [7:0] x2,
  input  [1:0] sel2,
  input  en2,
  input  [1:0] selc,
  input  [7:0] x3,
  input  [1:0] sel3,
  input  en3,
  input  [1:0] seld,
  input  rst,
  input  cf,
  input  rst_2,
  input  cf_2,
  input  rst_3,
  input  opr,
  output cf0,
  output cf1
);

  wire clk_out;
  wire [7:0] multiplexer_1_out, multiplexer_2_out, multiplexer_3_out, multiplexer_4_out, multiplexer_5_out,
       multiplexer_6_out, multiplexer_7_out, multiplexer_8_out, r0_s0_q, r1_s1_q, r2_s2_q, r3_s3_q;

  Clock clk (.out(clk_out));
  Multiplexer #(.select(2), .width(8), .enable("false")) multiplexer_1 (
    .in0(x0), .in1(multiplexer_2_out), .in2(multiplexer_3_out), .in3(multiplexer_4_out),
    .out(multiplexer_1_out), .sel(sel0));
  Multiplexer #(.select(2), .width(8), .enable("false")) multiplexer_2 (
    .in0(multiplexer_1_out), .in1(x1), .in2(multiplexer_3_out), .in3(multiplexer_4_out),
    .out(multiplexer_2_out), .sel(sel1));
  Multiplexer #(.select(2), .width(8), .enable("false")) multiplexer_3 (
    .in0(multiplexer_1_out), .in1(multiplexer_2_out), .in2(x2), .in3(multiplexer_4_out),
    .out(multiplexer_3_out), .sel(sel2));
  Multiplexer #(.select(2), .width(8), .enable("false")) multiplexer_4 (
    .in0(multiplexer_1_out), .in1(multiplexer_2_out), .in2(multiplexer_3_out), .in3(x3),
    .out(multiplexer_4_out), .sel(sel3));
  Register r0_s0 (.D(multiplexer_1_out), .en(clk_out), .Q(r0_s0_q), .clk(en0), .clr(rst));
  Register r1_s1 (.D(multiplexer_2_out), .en(clk_out), .Q(r1_s1_q), .clk(en1), .clr(rst));
  Register r2_s2 (.D(multiplexer_3_out), .en(clk_out), .Q(r2_s2_q), .clk(en2), .clr(rst));
  Register r3_s3 (.D(multiplexer_4_out), .en(clk_out), .Q(r3_s3_q), .clk(en3), .clr(rst));
  Control_Unit control_unit_1 (
    .cf(cf), .rst(rst_2));  // open: en0, en1, en2, en3, sel0, sel1, sel2, sel3, sela, selb, done
  Multiplexer #(.select(2), .width(8), .enable("false")) multiplexer_5 (
    .in0(r0_s0_q), .in1(r1_s1_q), .in2(r2_s2_q), .in3(r3_s3_q), .out(multiplexer_5_out), .sel(sela));
  Multiplexer #(.select(2), .width(8), .enable("false")) multiplexer_6 (
    .in0(r0_s0_q), .in1(r1_s1_q), .in2(r2_s2_q), .in3(r3_s3_q), .out(multiplexer_6_out), .sel(selb));
  Multiplexer #(.select(2), .width(8), .enable("false")) multiplexer_7 (
    .in0(r0_s0_q), .in1(r1_s1_q), .in2(r2_s2_q), .in3(r3_s3_q), .out(multiplexer_7_out), .sel(selc));
  Multiplexer #(.select(2), .width(8), .enable("false")) multiplexer_8 (
    .in0(r0_s0_q), .in1(r1_s1_q), .in2(r2_s2_q), .in3(r3_s3_q), .out(multiplexer_8_out), .sel(seld));
  Subtractor subtractor_1 (.a(multiplexer_5_out), .b(multiplexer_6_out), .bout(cf0));  // open: out, bin
  Subtractor subtractor_2 (.a(multiplexer_7_out), .b(multiplexer_8_out), .bout(cf1));  // open: out, bin
  cu cu_1 (.cf(cf_2), .rst(rst_3), .opr(opr));  // open: en0, en1, en2, en3, sel0, sel1, sel2, sel3, sela, selb, done

  // Notes on the sheet:
  //   en0-3,sel0-3,sela,selb,done
  //   Control Unit (with opr)
  //   en0-3,sel0-3,sela,selb,done
endmodule

module Control_Unit (
  input  cf,
  input  rst,
  output en0,
  output en1,
  output en2,
  output en3,
  output sel0,
  output sel1,
  output sel2,
  output sel3,
  output sela,
  output selb,
  output done
);

  Clock clk ();  // open: out
endmodule

module cu (
  input  cf,
  input  rst,
  input  opr,
  output en0,
  output en1,
  output en2,
  output en3,
  output sel0,
  output sel1,
  output sel2,
  output sel3,
  output sela,
  output selb,
  output done
);

  Clock clk ();  // open: out
endmodule
